// Logisim project assignment.circ as structural Verilog: 5 circuits, main circuit main
module main (
  input  in_1,
  input  in_2,
  input  in_3,
  input  in_4,
  input  in_5,
  input  in_6,
  output out_7,
  output out_8,
  output out_9,
  output out_10,
  output out_11
);

  wire register_1_out_6, register_1_out_7, register_1_out_8, register_1_out_9, register_1_out_10,
       register_1_out_11, register_1_out_12, register_1_out_13;

  Register register_1 (
    .in_1(in_1), .in_2(in_3), .in_3(in_4), .in_4(in_5), .in_5(in_6), .out_6(register_1_out_6),
    .out_7(register_1_out_7), .out_8(register_1_out_8), .out_9(register_1_out_9), .out_10(register_1_out_10),
    .out_11(register_1_out_11), .out_12(register_1_out_12), .out_13(register_1_out_13));
  _4_Bit_Adder u_4_bit_adder_1 (
    .in_1(in_2), .in_2(register_1_out_6), .in_3(register_1_out_7), .in_4(register_1_out_8),
    .in_5(register_1_out_9), .in_6(register_1_out_10), .in_7(register_1_out_11), .in_8(register_1_out_12),
    .in_9(register_1_out_13), .out_10(out_7), .out_11(out_8), .out_12(out_9), .out_13(out_10), .out_14(out_11));
  // AND_Gate and_1 is placed but not wired
endmodule

module FullAdder (
  input  A,
  input  B,
  input  C_out,
  output out_4,
  output out_5
);

  wire and_1_out, and_2_out, xor_1_out;

  xor xor_1 (xor_1_out, A, B);
  and and_1 (and_1_out, A, B);
  and and_2 (and_2_out, xor_1_out, C_out);
  or or_1 (out_4, and_1_out, and_2_out);
  xor xor_2 (out_5, xor_1_out, C_out);
endmodule

module _4_Bit_Adder (
  input  in_1,
  input  in_2,
  input  in_3,
  input  in_4,
  input  in_5,
  input  in_6,
  input  in_7,
  input  in_8,
  input  in_9,
  output out_10,
  output out_11,
  output out_12,
  output out_13,
  output out_14
);

  wire fulladder_2_out_4, fulladder_3_out_4, fulladder_4_out_4;

  FullAdder fulladder_1 (.A(in_5), .B(in_9), .C_out(fulladder_4_out_4), .out_4(out_13), .out_5(out_14));
  FullAdder fulladder_2 (.A(in_2), .B(in_6), .C_out(in_1), .out_4(fulladder_2_out_4), .out_5(out_10));
  FullAdder fulladder_3 (.A(in_3), .B(in_7), .C_out(fulladder_2_out_4), .out_4(fulladder_3_out_4), .out_5(out_11));
  FullAdder fulladder_4 (.A(in_4), .B(in_8), .C_out(fulladder_3_out_4), .out_4(fulladder_4_out_4), .out_5(out_12));
endmodule

module Store (
  input  in_1,
  input  in_2,
  input  in_3,
  input  in_4,
  input  in_5,
  output out_6,
  output out_7,
  output out_8,
  output out_9
);

  wire clock_1_out, not_1_out;

  Clock clock_1 (.out(clock_1_out));
  not not_1 (not_1_out, in_5);
  D_Flip_Flop d_ff_1 (.clk(clock_1_out), .D(in_1), .Q(out_6), .en(not_1_out));  // open: Qn, preset, reset
  D_Flip_Flop d_ff_2 (.clk(clock_1_out), .D(in_2), .Q(out_7), .en(not_1_out));  // open: Qn, preset, reset
  D_Flip_Flop d_ff_3 (.clk(clock_1_out), .D(in_3), .Q(out_8), .en(not_1_out));  // open: Qn, preset, reset
  D_Flip_Flop d_ff_4 (.clk(clock_1_out), .D(in_4), .Q(out_9), .en(not_1_out));  // open: Qn, preset, reset
endmodule

module Register (
  input  in_1,
  input  in_2,
  input  in_3,
  input  in_4,
  input  in_5,
  output out_6,
  output out_7,
  output out_8,
  output out_9,
  output out_10,
  output out_11,
  output out_12,
  output out_13
);

  assign out_10 = in_5 ? in_1 : 1'bz;  // Controlled_Buffer controlled_buffer_1
  assign out_11 = in_5 ? in_2 : 1'bz;  // Controlled_Buffer controlled_buffer_2
  assign out_12 = in_5 ? in_3 : 1'bz;  // Controlled_Buffer controlled_buffer_3
  assign out_13 = in_5 ? in_4 : 1'bz;  // Controlled_Buffer controlled_buffer_4
  Store store_1 (
    .in_1(in_1), .in_2(in_2), .in_3(in_3), .in_4(in_4), .in_5(in_5), .out_6(out_6), .out_7(out_7),
    .out_8(out_8), .out_9(out_9));
endmodule
